# Fritzing sketch 2LED (saved by Fritzing 0.9.3b)
breadboards: 1

parts:
  元件1 = Arduino Uno (Rev3)
  R1 = Resistor [tolerance=±5% resistance=220 package=THT]
  R2 = Resistor [tolerance=±5% resistance=220 package=THT]
  LED1 = LED - 5mm [color="Red (633nm)" package="5 mm [THT]"]
  LED2 = LED - 5mm [color="Red (633nm)" package="5 mm [THT]"]

nets:
  N1: 元件1.D8, R2.Pin_0
  N2: 元件1.D9_PWM, R1.Pin_0
  N3: 元件1.GND, LED1.anode, LED2.anode
  N4: R1.Pin_1, LED1.cathode
  N5: R2.Pin_1, LED2.cathode
